# Fritzing sketch PSoC5LP_MCP4922 (saved by Fritzing 0.9.3b)
breadboards: 3
perfboards: 2

parts:
  LCD1 = LCD screen
  R1 = Resistor [tolerance=±5% resistance=220 package=THT]
  R2 = TRIMPOT [package=3362u-2]
  U1 = Mini-USB _B_ connector with 5th pin broken out. [package=usb-minib]  # not connected
  XTAL1 = Crystal [frequency="16 Mhz" package=THT]
  C1 = Ceramic Capacitor [capacitance=100nF package="100 mil [THT, multilayer]"]
  C2 = Ceramic Capacitor [capacitance=100nF package="100 mil [THT, multilayer]"]
  IC1 = IC, DIP package, 14 pins [chip_label=MCP4922]
  C3 = Ceramic Capacitor [capacitance=100nF package="100 mil [THT, multilayer]"]

nets:
  N1: LCD1.VSS, R1.Pin_0, R2.CW
  N2: LCD1.VDD, R2.WIPER
  N3: LCD1.LED+, R1.Pin_1
  N4: LCD1.LED-, R2.CCW
  N5: XTAL1.pin_0, C1.0
  N6: XTAL1.pin_1, C2.1
  N7: C1.1, C2.0, IC1.pin8, IC1.pin12, C3.0
  N8: IC1.pin1, IC1.pin9, IC1.pin11, IC1.pin13, C3.1

notes:
  PSoC 5 LP
  Prototyping Kit
  VOUTA (MCP4922)
  MCP4922
  1 VDD 14 OUTA
  2 NC 13 VREFA
  3 !CS 12 AVSS
  4 SCK 11 VREFB
  5 SDI 10 VOUTB
  6 NC 9 !SHDN
  7 NC 8 LDAC
  VOUT (VDAC8)
